// Logisim project ALU.circ as structural Verilog: 2 circuits, main circuit main
module main (
  input  [3:0] in_1,
  input  [3:0] in_2,
  input  [1:0] in_3,
  output [3:0] out_4
);

  wire [3:0] adder_1_out, and_1_out, or_1_out, subtractor_1_out;

  Adder #(.width(4)) adder_1 (.a(in_1), .b(in_2), .out(adder_1_out));  // open: cin, cout
  Subtractor #(.width(4)) subtractor_1 (.a(in_1), .b(in_2), .out(subtractor_1_out));  // open: bin, bout
  assign and_1_out = in_1 & in_2;  // AND_Gate and_1, 4 bits wide
  assign or_1_out = in_1 | in_2;  // OR_Gate or_1, 4 bits wide
  Multiplexer #(.select(2), .width(4)) multiplexer_1 (
    .in0(adder_1_out), .in1(subtractor_1_out), .in2(and_1_out), .in3(or_1_out), .out(out_4), .sel(in_3));  // open: en

  // Other names for the same wires on the sheet: A[3:0] = in_1; B[3:0] = in_2
endmodule

module alu (
  input  [3:0] in_1,
  input  [3:0] in_2,
  input  [1:0] in_3,
  output [3:0] out_4
);

  wire [3:0] adder_1_out, and_1_out, or_1_out, subtractor_1_out;

  Adder #(.width(4)) adder_1 (.a(in_1), .b(in_2), .out(adder_1_out));  // open: cin, cout
  Subtractor #(.width(4)) subtractor_1 (.a(in_1), .b(in_2), .out(subtractor_1_out));  // open: bin, bout
  assign and_1_out = in_1 & in_2;  // AND_Gate and_1, 4 bits wide
  assign or_1_out = in_1 | in_2;  // OR_Gate or_1, 4 bits wide
  Multiplexer #(.select(2), .width(4)) multiplexer_1 (
    .in0(adder_1_out), .in1(subtractor_1_out), .in2(and_1_out), .in3(or_1_out), .out(out_4), .sel(in_3));  // open: en

  // Other names for the same wires on the sheet: A[3:0] = in_1; B[3:0] = in_2
endmodule
