// Logisim project CRC.circ as structural Verilog
module _4bit_divider (
  input  [3:0] beichu,
  input  [3:0] chu,
  output [2:0] out_3
);

  wire [3:0] xor_1_out;

  assign xor_1_out = beichu ^ chu;  // XOR_Gate xor_1, 4 bits wide
  Multiplexer #(.width(3)) multiplexer_1 (
    .in0(beichu[2:0]), .in1(xor_1_out[2:0]), .out(out_3), .sel(beichu[3]));  // open: en
endmodule

module CRC (
  input  [7:0] in_1,
  input  [3:0] in_2,
  output [10:0] out_3
);

  wire [2:0] re1, re2, re3, re4, re5, re6, re7;

  // Probe on {in_1, 3'b000}
  // Probe on re1
  _4bit_divider u_4bit_divider_1 (.beichu(in_1[7:4]), .chu(in_2), .out_3(re1));
  // Probe on re2
  _4bit_divider u_4bit_divider_2 (.beichu({re1, in_1[3]}), .chu(in_2), .out_3(re2));
  // Probe on re3
  _4bit_divider u_4bit_divider_3 (.beichu({re2, in_1[2]}), .chu(in_2), .out_3(re3));
  // Probe on re4
  _4bit_divider u_4bit_divider_4 (.beichu({re3, in_1[1]}), .chu(in_2), .out_3(re4));
  // Probe on re5
  _4bit_divider u_4bit_divider_5 (.beichu({re4, in_1[0]}), .chu(in_2), .out_3(re5));
  // Probe on re6
  _4bit_divider u_4bit_divider_6 (.beichu({re5, 1'b0}), .chu(in_2), .out_3(re6));
  // Probe on re7
  _4bit_divider u_4bit_divider_7 (.beichu({re6, 1'b0}), .chu(in_2), .out_3(re7));
  // Probe on out_3[2:0]
  _4bit_divider u_4bit_divider_8 (.beichu({re7, 1'b0}), .chu(in_2), .out_3(out_3[2:0]));

  assign out_3[10:3] = in_1;

  // Other names for the same wires on the sheet: chu[3:0] = in_2; re8[2:0] = out_3[2:0]; _3 = in_1[0];
  //   bc[10:3] = in_1; bc_pre[7:0] = in_1; _4 = in_1[1]; _5 = in_1[2]; _6 = in_1[3]
endmodule

module sequential_CRC (
  input  [7:0] in_1,
  input  [3:0] in_2,
  output [2:0] out_3
);

  wire clock_1_out, clock_2_out, clock_3_out, clock_4_out, register_1_q, register_2_q;
  wire [0:0] in;
  wire [2:0] n4bit_divider_1_out_3;
  wire [3:0] multiplexer_2_out;
  wire [9:0] register_3_q;
  wire [10:0] multiplexer_1_out, shifter_1_out, shifter_2_out;

  Clock clock_1 (.out(clock_1_out));
  Shifter #(.width(11)) shifter_1 (.in({in_1, 3'b000}), .\dist (4'b0011), .out(shifter_1_out));
  Register #(.width(1)) register_1 (.D(1'b1), .Q(register_1_q), .clk(clock_2_out));  // open: en, clr
  Clock clock_2 (.out(clock_2_out));
  Register #(.width(1)) register_2 (.D(1'b1), .Q(register_2_q), .clk(clock_1_out));  // open: en, clr
  Multiplexer #(.width(11)) multiplexer_1 (
    .in0(shifter_1_out), .in1({in[0], register_3_q}), .out(multiplexer_1_out), .sel(register_1_q));  // open: en
  // Probe on shifter_2_out
  Shifter #(.width(11)) shifter_2 (.in(multiplexer_1_out), .\dist (4'b0001), .out(shifter_2_out));
  Register #(.width(11)) register_3 (.D(shifter_2_out), .Q({in[0], register_3_q}), .clk(clock_3_out));  // open: en, clr
  Clock clock_3 (.out(clock_3_out));
  Multiplexer #(.width(4)) multiplexer_2 (
    .in0(in_1[7:4]), .in1({out_3, in[0]}), .out(multiplexer_2_out), .sel(register_2_q));  // open: en
  // Probe on in[0]
  // Probe on {in[0], register_3_q}
  _4bit_divider u_4bit_divider_1 (.beichu(multiplexer_2_out), .chu(in_2), .out_3(n4bit_divider_1_out_3));
  Clock clock_4 (.out(clock_4_out));
  Register #(.width(3)) register_4 (.D(n4bit_divider_1_out_3), .Q(out_3), .clk(clock_4_out));  // open: en, clr

  // Other names for the same wires on the sheet: chu[3:0] = in_2; in[3:1] = out_3
endmodule

module combinatorial_CRC (
  input  [7:0] in_1,
  input  [3:0] in_2,
  output [2:0] out_3
);

  wire [2:0] re1, re2, re3, re4, re5, re6, re7;

  // Probe on {in_1, 3'b000}
  // Probe on re1
  _4bit_divider u_4bit_divider_1 (.beichu(in_1[7:4]), .chu(in_2), .out_3(re1));
  // Probe on re2
  _4bit_divider u_4bit_divider_2 (.beichu({re1, in_1[3]}), .chu(in_2), .out_3(re2));
  // Probe on re3
  _4bit_divider u_4bit_divider_3 (.beichu({re2, in_1[2]}), .chu(in_2), .out_3(re3));
  // Probe on re4
  _4bit_divider u_4bit_divider_4 (.beichu({re3, in_1[1]}), .chu(in_2), .out_3(re4));
  // Probe on re5
  _4bit_divider u_4bit_divider_5 (.beichu({re4, in_1[0]}), .chu(in_2), .out_3(re5));
  // Probe on re6
  _4bit_divider u_4bit_divider_6 (.beichu({re5, 1'b0}), .chu(in_2), .out_3(re6));
  // Probe on re7
  _4bit_divider u_4bit_divider_7 (.beichu({re6, 1'b0}), .chu(in_2), .out_3(re7));
  // Probe on out_3
  _4bit_divider u_4bit_divider_8 (.beichu({re7, 1'b0}), .chu(in_2), .out_3(out_3));

  // Other names for the same wires on the sheet: _3 = in_1[0]; bc[10:3] = in_1; _4 = in_1[1]; _5 = in_1[2];
  //   _6 = in_1[3]; chu[3:0] = in_2; re8[2:0] = out_3
endmodule
