// Logisim project FSM.circ as structural Verilog
module fsm (
  input  clr,
  input  [1:0] in_2,
  output out_3
);

  wire clock_1_out, comparator_1_eq, comparator_2_eq;
  wire [1:0] register_1_q, transition_1_out_4;

  transition transition_1 (.clr(clr), .s0(register_1_q), .in(in_2), .out_4(transition_1_out_4));
  Register #(.width(2)) register_1 (.D(transition_1_out_4), .Q(register_1_q), .clk(clock_1_out));  // open: en, clr
  Clock clock_1 (.out(clock_1_out));
  Comparator #(.width(2), .mode("unsigned")) comparator_1 (
    .a(transition_1_out_4), .b(2'b10), .eq(comparator_1_eq));  // open: gt, lt
  Comparator #(.width(2), .mode("unsigned")) comparator_2 (
    .a(transition_1_out_4), .b(2'b11), .eq(comparator_2_eq));  // open: gt, lt
  or or_1 (out_3, comparator_1_eq, comparator_2_eq);
endmodule

module transition (
  input  clr,
  input  [1:0] s0,
  input  [1:0] in,
  output [1:0] out_4
);

  wire and_1_out, and_2_out, and_3_out, and_4_out, not_1_out, not_2_out, not_3_out, not_4_out, not_5_out,
       not_6_out, not_7_out;
  wire [1:0] multiplexer_1_out;

  Multiplexer #(.width(2)) multiplexer_1 (.in0(s0), .in1(2'b00), .out(multiplexer_1_out), .sel(clr));  // open: en
  not not_1 (not_1_out, multiplexer_1_out[1]);
  not not_2 (not_2_out, in[0]);
  not not_3 (not_3_out, multiplexer_1_out[0]);
  not not_4 (not_4_out, in[0]);
  not not_5 (not_5_out, in[1]);
  not not_6 (not_6_out, multiplexer_1_out[0]);
  not not_7 (not_7_out, in[0]);
  and and_1 (and_1_out, not_1_out, multiplexer_1_out[0], not_2_out);
  and and_2 (and_2_out, multiplexer_1_out[1], not_3_out, not_4_out);
  and and_3 (and_3_out, not_5_out, in[0]);
  and and_4 (and_4_out, multiplexer_1_out[1], not_6_out, not_7_out);
  or or_1 (out_4[1], and_1_out, and_2_out);
  or or_2 (out_4[0], and_3_out, and_4_out);
endmodule
