// Logisim project FSM_qql.circ as structural Verilog: 3 circuits, main circuit fsm
module fsm (
  input  [1:0] in,
  input  clr,
  output out_3
);

  wire clock_1_out, register_1_q;
  wire [1:0] S_q;
  wire [1:1] statran_1_out_5;

  Clock clock_1 (.out(clock_1_out));
  statran statran_1 (
    .sn0(S_q[0]), .sn1(S_q[1]), .in0(in[1]), .in1(in[1]), .out_5(statran_1_out_5[1]),
    .out_6(statran_1_out_5[1]));
  Register #(.width(1)) register_1 (.D(clr), .Q(register_1_q), .clk(clock_1_out), .clr(register_1_q));  // open: en
  Register #(.width(2)) S (.D({2{statran_1_out_5[1]}}), .Q(S_q), .clk(clock_1_out), .clr(register_1_q));  // open: en
  z z_1 (.s0(statran_1_out_5[1]), .s1(statran_1_out_5[1]), .in0(in[1]), .z(out_3));

  assign in[0] = in[1];
endmodule

module z (
  input  s0,
  input  s1,
  input  in0,
  output z
);

  wire not_1_out, not_2_out;

  not not_1 (not_1_out, s0);
  not not_2 (not_2_out, in0);
  and and_1 (z, not_1_out, s1, not_2_out);
endmodule

module statran (
  input  sn0,
  input  sn1,
  input  in0,
  input  in1,
  output out_5,
  output out_6
);

  wire and_1_out, and_2_out, and_3_out, not_1_out, not_2_out, not_3_out, not_4_out;

  not not_1 (not_1_out, sn0);
  not not_2 (not_2_out, in0);
  not not_3 (not_3_out, sn1);
  not not_4 (not_4_out, in1);
  and and_1 (and_1_out, not_1_out, sn1, not_2_out);
  and and_2 (and_2_out, not_2_out, not_3_out, sn0);
  and and_3 (and_3_out, not_4_out, in0);
  or sn_0 (out_5, and_1_out, and_3_out);
  or sn_1 (out_6, and_1_out, and_2_out);
endmodule
