// Logisim project GRF.circ as structural Verilog: 6 circuits, main circuit 4reg
module _4reg (
  input  clk,
  input  reset,
  input  WE,
  input  EN4_3,
  input  [1:0] A14,
  input  [1:0] A24,
  input  [1:0] A34,
  input  [31:0] WD,
  output [31:0] RD1,
  output [31:0] RD2
);

  wire and_1_out, not_1_out;
  wire [31:0] n2reg_1_rd1, n2reg_1_rd2, n2reg_2_rd1, n2reg_2_rd2;

  and and_1 (and_1_out, WE, EN4_3);
  not not_1 (not_1_out, A34[1]);
  _2reg u_2reg_1 (
    .A15(A14[0]), .A25(A24[0]), .A35(A34[0]), .WD(WD), .clk(clk), .reset(reset), .WE(and_1_out),
    .EN5_4(not_1_out), .RD1(n2reg_1_rd1), .RD2(n2reg_1_rd2));
  _2reg u_2reg_2 (
    .A15(A14[0]), .A25(A24[0]), .A35(A34[0]), .WD(WD), .clk(clk), .reset(reset), .WE(and_1_out),
    .EN5_4(A34[1]), .RD1(n2reg_2_rd1), .RD2(n2reg_2_rd2));
  Multiplexer #(.width(32)) multiplexer_1 (.in0(n2reg_1_rd1), .in1(n2reg_2_rd1), .out(RD1), .sel(A14[1]));  // open: en
  Multiplexer #(.width(32)) multiplexer_2 (.in0(n2reg_1_rd2), .in1(n2reg_2_rd2), .out(RD2), .sel(A24[1]));  // open: en

  // Other names for the same wires on the sheet: slt1_4 = A14[1]; slt2_4 = A24[1]; EN4_4 = A34[1]
endmodule

module _8reg (
  input  clk,
  input  reset,
  input  WE,
  input  EN3_2,
  input  [2:0] A13,
  input  [2:0] A23,
  input  [2:0] A33,
  input  [31:0] WD,
  output [31:0] RD1,
  output [31:0] RD2
);

  wire and_1_out, not_1_out;
  wire [31:0] n4reg_1_rd1, n4reg_1_rd2, n4reg_2_rd1, n4reg_2_rd2;

  and and_1 (and_1_out, WE, EN3_2);
  not not_1 (not_1_out, A33[2]);
  _4reg u_4reg_1 (
    .A14(A13[1:0]), .A24(A23[1:0]), .A34(A33[1:0]), .WD(WD), .clk(clk), .reset(reset), .WE(and_1_out),
    .EN4_3(not_1_out), .RD1(n4reg_1_rd1), .RD2(n4reg_1_rd2));
  _4reg u_4reg_2 (
    .A14(A13[1:0]), .A24(A23[1:0]), .A34(A33[1:0]), .WD(WD), .clk(clk), .reset(reset), .WE(and_1_out),
    .EN4_3(A33[2]), .RD1(n4reg_2_rd1), .RD2(n4reg_2_rd2));
  Multiplexer #(.width(32)) multiplexer_1 (.in0(n4reg_1_rd1), .in1(n4reg_2_rd1), .out(RD1), .sel(A13[2]));  // open: en
  Multiplexer #(.width(32)) multiplexer_2 (.in0(n4reg_1_rd2), .in1(n4reg_2_rd2), .out(RD2), .sel(A23[2]));  // open: en

  // Other names for the same wires on the sheet: slt1_3 = A13[2]; slt2_3 = A23[2]; EN3_3 = A33[2]
endmodule

module _2reg (
  input  clk,
  input  reset,
  input  WE,
  input  EN5_4,
  input  A15,
  input  A25,
  input  A35,
  input  [31:0] WD,
  output [31:0] RD1,
  output [31:0] RD2
);

  wire and_1_out, and_2_out, and_3_out, not_1_out;
  wire [31:0] _0_2_q, _0_q;

  and and_1 (and_1_out, WE, EN5_4);
  not not_1 (not_1_out, A35);
  and and_2 (and_2_out, and_1_out, not_1_out);
  and and_3 (and_3_out, and_1_out, A35);
  Register #(.width(32)) _0 (.D(WD), .en(and_2_out), .Q(_0_q), .clk(clk), .clr(reset));
  Register #(.width(32)) _0_2 (.D(WD), .en(and_3_out), .Q(_0_2_q), .clk(clk), .clr(reset));
  Multiplexer #(.width(32)) multiplexer_1 (.in0(_0_q), .in1(_0_2_q), .out(RD1), .sel(A15));  // open: en
  Multiplexer #(.width(32)) multiplexer_2 (.in0(_0_q), .in1(_0_2_q), .out(RD2), .sel(A25));  // open: en
endmodule

module _16reg (
  input  clk,
  input  reset,
  input  WE,
  input  EN2_1,
  input  [3:0] A12,
  input  [3:0] A22,
  input  [3:0] A32,
  input  [31:0] WD,
  output [31:0] RD1,
  output [31:0] RD2
);

  wire and_1_out, not_1_out;
  wire [31:0] n8reg_1_rd1, n8reg_1_rd2, n8reg_2_rd1, n8reg_2_rd2;

  and and_1 (and_1_out, WE, EN2_1);
  not not_1 (not_1_out, A32[3]);
  _8reg u_8reg_1 (
    .A13(A12[2:0]), .A23(A22[2:0]), .A33(A32[2:0]), .WD(WD), .clk(clk), .reset(reset), .WE(and_1_out),
    .EN3_2(not_1_out), .RD1(n8reg_1_rd1), .RD2(n8reg_1_rd2));
  _8reg u_8reg_2 (
    .A13(A12[2:0]), .A23(A22[2:0]), .A33(A32[2:0]), .WD(WD), .clk(clk), .reset(reset), .WE(and_1_out),
    .EN3_2(A32[3]), .RD1(n8reg_2_rd1), .RD2(n8reg_2_rd2));
  Multiplexer #(.width(32)) multiplexer_1 (.in0(n8reg_1_rd1), .in1(n8reg_2_rd1), .out(RD1), .sel(A12[3]));  // open: en
  Multiplexer #(.width(32)) multiplexer_2 (.in0(n8reg_1_rd2), .in1(n8reg_2_rd2), .out(RD2), .sel(A22[3]));  // open: en

  // Other names for the same wires on the sheet: slt1_2 = A12[3]; slt2_2 = A22[3]; EN2_2 = A32[3]
endmodule

module _32reg (
  input  clk,
  input  reset,
  input  WE,
  input  [4:0] A11,
  input  [4:0] A21,
  input  [4:0] A31,
  input  [31:0] WD,
  output [31:0] RD1,
  output [31:0] RD2
);

  wire not_1_out, pd;
  wire [31:0] multiplexer_1_out, n16reg_1_rd1, n16reg_1_rd2, n16reg_2_rd1, n16reg_2_rd2;

  Multiplexer #(.width(32)) multiplexer_1 (.in0(WD), .in1({32{1'b0}}), .out(multiplexer_1_out), .sel(pd));  // open: en
  Comparator #(.width(5), .mode("unsigned")) comparator_1 (.a(A31), .b({5{1'b0}}), .eq(pd));  // open: gt, lt
  not not_1 (not_1_out, A31[4]);
  _16reg u_16reg_1 (
    .A12(A11[3:0]), .A22(A21[3:0]), .A32(A31[3:0]), .WD(multiplexer_1_out), .clk(clk), .reset(reset),
    .WE(WE), .EN2_1(not_1_out), .RD1(n16reg_1_rd1), .RD2(n16reg_1_rd2));
  _16reg u_16reg_2 (
    .A12(A11[3:0]), .A22(A21[3:0]), .A32(A31[3:0]), .WD(multiplexer_1_out), .clk(clk), .reset(reset),
    .WE(WE), .EN2_1(A31[4]), .RD1(n16reg_2_rd1), .RD2(n16reg_2_rd2));
  Multiplexer #(.width(32)) multiplexer_2 (
    .in0(n16reg_1_rd1), .in1(n16reg_2_rd1), .out(RD1), .sel(A11[4]));  // open: en
  Multiplexer #(.width(32)) multiplexer_3 (
    .in0(n16reg_1_rd2), .in1(n16reg_2_rd2), .out(RD2), .sel(A21[4]));  // open: en

  // Other names for the same wires on the sheet: slt1_1 = A11[4]; slt2_1 = A21[4]; EN1_1 = A31[4]
endmodule

module grf (
  input  clk,
  input  reset,
  input  WE,
  input  [4:0] A11,
  input  [4:0] A21,
  input  [4:0] A31,
  input  [31:0] WD,
  output [31:0] RD1,
  output [31:0] RD2
);

  wire not_1_out, pd;
  wire [31:0] multiplexer_1_out, n16reg_1_rd1, n16reg_1_rd2, n16reg_2_rd1, n16reg_2_rd2;

  Multiplexer #(.width(32)) multiplexer_1 (.in0(WD), .in1({32{1'b0}}), .out(multiplexer_1_out), .sel(pd));  // open: en
  Comparator #(.width(5), .mode("unsigned")) comparator_1 (.a(A31), .b({5{1'b0}}), .eq(pd));  // open: gt, lt
  not not_1 (not_1_out, A31[4]);
  _16reg u_16reg_1 (
    .A12(A11[3:0]), .A22(A21[3:0]), .A32(A31[3:0]), .WD(multiplexer_1_out), .clk(clk), .reset(reset),
    .WE(WE), .EN2_1(not_1_out), .RD1(n16reg_1_rd1), .RD2(n16reg_1_rd2));
  _16reg u_16reg_2 (
    .A12(A11[3:0]), .A22(A21[3:0]), .A32(A31[3:0]), .WD(multiplexer_1_out), .clk(clk), .reset(reset),
    .WE(WE), .EN2_1(A31[4]), .RD1(n16reg_2_rd1), .RD2(n16reg_2_rd2));
  Multiplexer #(.width(32)) multiplexer_2 (
    .in0(n16reg_1_rd1), .in1(n16reg_2_rd1), .out(RD1), .sel(A11[4]));  // open: en
  Multiplexer #(.width(32)) multiplexer_3 (
    .in0(n16reg_1_rd2), .in1(n16reg_2_rd2), .out(RD2), .sel(A21[4]));  // open: en

  // Other names for the same wires on the sheet: slt1_1 = A11[4]; slt2_1 = A21[4]; EN1_1 = A31[4]
endmodule
