// Logisim project P3.circ as structural Verilog: 9 circuits, main circuit main
module main (
  input  Reset,
  output [31:0] out_2,
  output out_3,
  output [4:0] out_4,
  output [31:0] out_5,
  output out_6,
  output [4:0] out_7,
  output [31:0] out_8
);

  wire ALUSrc, clock_1_out, clock_2_out, clock_3_out, jal, jal_r, jr, jump, lb, MemtoReg, nPC_sel, RegDst,
       sb, sll, zero;
  wire [1:0] ExtOp;
  wire [2:0] ALUctr;
  wire [4:0] multiplexer_1_out;
  wire [31:0] busA, dm_1_dmout, ext_1_out_3, jrPC, multiplexer_3_out, multiplexer_4_out, PC_4;

  Clock clock_1 (.out(clock_1_out));
  Multiplexer #(.width(5)) multiplexer_1 (
    .in0(out_2[20:16]), .in1(out_2[15:11]), .out(multiplexer_1_out), .sel(RegDst));  // open: en
  Multiplexer #(.width(5)) multiplexer_2 (
    .in0(multiplexer_1_out), .in1({5{1'b1}}), .out(out_4), .sel(jal));  // open: en
  GRF grf_1 (
    .busW(out_5), .busA(busA), .busB(out_8), .RegWr(out_3), .RW(out_4), .RA(out_2[25:21]), .RB(out_2[20:16]),
    .clk(clock_2_out), .reset(Reset));
  Clock clock_2 (.out(clock_2_out));
  IFU IFU (
    .nPC_sel(nPC_sel), .zero(zero), .imm16(out_2[15:0]), .clr(Reset), .clk(clock_1_out), .instr(out_2),
    .jump(jump), .imm28({out_2[25:0], 2'b00}), .PC_4(PC_4), .jrPC({jrPC[31:7], out_7, jrPC[1:0]}), .jr(jr));
  Multiplexer #(.width(32)) multiplexer_3 (
    .in0(out_8), .in1(ext_1_out_3), .out(multiplexer_3_out), .sel(ALUSrc));  // open: en
  EXT ext_1 (.imm16(out_2[15:0]), .out_3(ext_1_out_3), .ExtOp(ExtOp));
  ALU alu_1 (
    .ALUin1(busA), .ALUin2(multiplexer_3_out), .ALUOut({jrPC[31:7], out_7, jrPC[1:0]}), .zero(zero),
    .ALUctr(ALUctr), .ALUin1_prime(out_8), .sll(sll));
  Clock clock_3 (.out(clock_3_out));
  DM dm_1 (
    .DMdata(out_8), .clk(clock_3_out), .DMOut(dm_1_dmout), .MemWr(out_6),
    .DMaddr({jrPC[31:7], out_7, jrPC[1:0]}), .reset(Reset), .sb(sb), .lb(lb));
  Multiplexer #(.width(32)) multiplexer_4 (
    .in0({jrPC[31:7], out_7, jrPC[1:0]}), .in1(dm_1_dmout), .out(multiplexer_4_out), .sel(MemtoReg));  // open: en
  Multiplexer #(.width(32)) multiplexer_5 (.in0(multiplexer_4_out), .in1(PC_4), .out(out_5), .sel(jal_r));  // open: en
  Controller controller_1 (
    .opcode(out_2[31:26]), .funct(out_2[5:0]), .ALUSrc(ALUSrc), .nPC_sel(nPC_sel), .MemWr(out_6),
    .MemtoReg(MemtoReg), .RegDst(RegDst), .RegWr(out_3), .ExtOp(ExtOp), .ALUctr(ALUctr), .jump(jump),
    .jal_r(jal_r), .sll(sll), .jr(jr), .jal(jal), .sb(sb), .lb(lb));

  // Other names for the same wires on the sheet: busB[31:0] = out_8; MemData[31:0] = out_8; funct[5:0] = out_2[5:0];
  //   imm16[15:0] = out_2[15:0]; imm28[27:2] = out_2[25:0]; instr[31:0] = out_2; shamt[4:0] = out_2[10:6];
  //   rd[4:0] = out_2[15:11]; rt[4:0] = out_2[20:16]; rs[4:0] = out_2[25:21]; opcode[5:0] = out_2[31:26];
  //   MemAddr[31:0] = {jrPC[31:7], out_7, jrPC[1:0]}; jrPC[6:2] = out_7; MemWr = out_6; RegAddr[4:0] = out_4;
  //   RegData[31:0] = out_5; RegWr = out_3
endmodule

module IFU (
  input  nPC_sel,
  input  zero,
  input  jump,
  input  jr,
  input  [15:0] imm16,
  input  [27:0] imm28,
  input  [31:0] jrPC,
  input  clr,
  input  clk,
  output [31:0] instr,
  output [31:0] PC_4
);

  wire and_1_out;
  wire [4:0] PC_q_2;
  wire [27:0] adder_1_out;
  wire [31:0] adder_2_out, bit_extender_1_out, multiplexer_1_out, multiplexer_2_out, multiplexer_3_out, PC_q,
       subtractor_1_out, subtractor_2_out;
  wire [31:28] adder_1_out_2;

  assign bit_extender_1_out = {{14{imm16[15]}}, {imm16, 2'b00}};  // Bit_Extender bit_extender_1
  and and_1 (and_1_out, nPC_sel, zero);
  Adder #(.width(32)) adder_1 (
    .a(32'h4), .b({PC_q[31:7], PC_q_2, PC_q[1:0]}), .out({adder_1_out_2, adder_1_out}));  // open: cin, cout
  Adder #(.width(32)) adder_2 (
    .a({adder_1_out_2, adder_1_out}), .b(bit_extender_1_out), .out(adder_2_out));  // open: cin, cout
  Multiplexer #(.width(32)) multiplexer_1 (
    .in0({adder_1_out_2, adder_1_out}), .in1(adder_2_out), .out(multiplexer_1_out), .sel(and_1_out));  // open: en
  Multiplexer #(.width(32)) multiplexer_2 (
    .in0(multiplexer_1_out), .in1(subtractor_1_out), .out(multiplexer_2_out), .sel(jump));  // open: en
  Subtractor #(.width(32)) subtractor_1 (
    .a({adder_1_out_2, imm28}), .b(32'h3000), .out(subtractor_1_out));  // open: bin, bout
  Subtractor #(.width(32)) subtractor_2 (.a(jrPC), .b(32'h3000), .out(subtractor_2_out));  // open: bin, bout
  Multiplexer #(.width(32)) multiplexer_3 (
    .in0(multiplexer_2_out), .in1(subtractor_2_out), .out(multiplexer_3_out), .sel(jr));  // open: en
  Register #(.width(32)) PC (
    .D(multiplexer_3_out), .Q({PC_q[31:7], PC_q_2, PC_q[1:0]}), .clk(clk), .clr(clr));  // open: en
  ROM #(.addrWidth(5), .dataWidth(32)) rom_1 (.addr(PC_q_2), .data(instr));  // open: sel
  Adder #(.width(32)) adder_3 (.a({adder_1_out_2, adder_1_out}), .b(32'h3000), .out(PC_4));  // open: cin, cout

  // Notes on the sheet:
  //   contents of rom_1 (hex, n*v repeats v):
  //   34840004 3c081234 35085678 ac880000 3529ccdd a0890001 80850001 80860002
endmodule

// RegFile
module GRF (
  input  RegWr,
  input  clk,
  input  reset,
  input  [4:0] RA,
  input  [4:0] RW,
  input  [4:0] RB,
  input  [31:0] busW,
  output [31:0] busA,
  output [31:0] busB
);

  wire undriven, undriven_2;
  wire [31:0] demultiplexer_1_out0, i1, i2, i3, i4, i5, i6, i7, i8, i9, i10, i11, i12, i13, i14, i15, i16,
       i17, i18, i19, i20, i21, i22, i23, i24, i25, i26, i27, i28, i29, i30, i31, o0, o1, o2, o3, o4, o5, o6,
       o7, o8, o9, o10, o11, o12, o13, o14, o15, o16, o17, o18, o19, o20, o21, o22, o23, o24, o25, o26, o27,
       o28, o29, o30, o31;

  Register #(.width(32)) register_1 (.D({32{1'b0}}), .en(RegWr), .Q(o0), .clk(clk), .clr(reset));
  Register #(.width(32)) register_2 (.D(i8), .en(RegWr), .Q(o8), .clk(clk), .clr(reset));
  Register #(.width(32)) register_3 (.D(i16), .en(RegWr), .Q(o16), .clk(clk), .clr(reset));
  Register #(.width(32)) register_4 (.D(i24), .en(RegWr), .Q(o24), .clk(clk), .clr(reset));
  Register #(.width(32)) register_5 (.D(i1), .en(RegWr), .Q(o1), .clk(clk), .clr(reset));
  Register #(.width(32)) register_6 (.D(i9), .en(RegWr), .Q(o9), .clk(clk), .clr(reset));
  Register #(.width(32)) register_7 (.D(i17), .en(RegWr), .Q(o17), .clk(clk), .clr(reset));
  Register #(.width(32)) register_8 (.D(i25), .en(RegWr), .Q(o25), .clk(clk), .clr(reset));
  Demultiplexer #(.select(5), .width(32), .tristate("true")) demultiplexer_1 (
    .out0(demultiplexer_1_out0), .out1(i1), .out2(i2), .out3(i3), .out4(i4), .out5(i5), .out6(i6), .out7(i7),
    .out8(i8), .out9(i9), .out10(i10), .out11(i11), .out12(i12), .out13(i13), .out14(i14), .out15(i15),
    .out16(i16), .out17(i17), .out18(i18), .out19(i19), .out20(i20), .out21(i21), .out22(i22), .out23(i23),
    .out24(i24), .out25(i25), .out26(i26), .out27(i27), .out28(i28), .out29(i29), .out30(i30), .out31(i31),
    .in(busW), .sel(RW));  // open: en
  Register #(.width(32)) register_9 (.D(i2), .en(RegWr), .Q(o2), .clk(clk), .clr(reset));
  Register #(.width(32)) register_10 (.D(i10), .en(RegWr), .Q(o10), .clk(clk), .clr(reset));
  Register #(.width(32)) register_11 (.D(i18), .en(RegWr), .Q(o18), .clk(clk), .clr(reset));
  Register #(.width(32)) register_12 (.D(i26), .en(RegWr), .Q(o26), .clk(clk), .clr(reset));
  Register #(.width(32)) register_13 (.D(i3), .en(RegWr), .Q(o3), .clk(clk), .clr(reset));
  Register #(.width(32)) register_14 (.D(i11), .en(RegWr), .Q(o11), .clk(clk), .clr(reset));
  Register #(.width(32)) register_15 (.D(i19), .en(RegWr), .Q(o19), .clk(clk), .clr(reset));
  Register #(.width(32)) register_16 (.D(i27), .en(RegWr), .Q(o27), .clk(clk), .clr(reset));
  Register #(.width(32)) register_17 (.D(i4), .en(RegWr), .Q(o4), .clk(clk), .clr(reset));
  Register #(.width(32)) register_18 (.D(i12), .en(RegWr), .Q(o12), .clk(clk), .clr(reset));
  Register #(.width(32)) register_19 (.D(i20), .en(RegWr), .Q(o20), .clk(clk), .clr(reset));
  Register #(.width(32)) register_20 (.D(i28), .en(RegWr), .Q(o28), .clk(clk), .clr(reset));
  Register #(.width(32)) register_21 (.D(i5), .en(RegWr), .Q(o5), .clk(clk), .clr(reset));
  Register #(.width(32)) register_22 (.D(i13), .en(RegWr), .Q(o13), .clk(clk), .clr(reset));
  Register #(.width(32)) register_23 (.D(i21), .en(RegWr), .Q(o21), .clk(clk), .clr(reset));
  Register #(.width(32)) register_24 (.D(i29), .en(RegWr), .Q(o29), .clk(clk), .clr(reset));
  Multiplexer #(.select(5), .width(32)) multiplexer_1 (
    .in0(o0), .in1(o1), .in2(o2), .in3(o3), .in4(o4), .in5(o5), .in6(o6), .in7(o7), .in8(o8), .in9(o9),
    .in10(o10), .in11(o11), .in12(o12), .in13(o13), .in14(o14), .in15(o15), .in16(o16), .in17(o17),
    .in18(o18), .in19(o19), .in20(o20), .in21(o21), .in22(o22), .in23(o23), .in24(o24), .in25(o25),
    .in26(o26), .in27(o27), .in28(o28), .in29(o29), .in30(o30), .in31(o31), .out(busA), .sel(RA),
    .en(undriven));
  Register #(.width(32)) register_25 (.D(i6), .en(RegWr), .Q(o6), .clk(clk), .clr(reset));
  Register #(.width(32)) register_26 (.D(i14), .en(RegWr), .Q(o14), .clk(clk), .clr(reset));
  Register #(.width(32)) register_27 (.D(i22), .en(RegWr), .Q(o22), .clk(clk), .clr(reset));
  Register #(.width(32)) register_28 (.D(i30), .en(RegWr), .Q(o30), .clk(clk), .clr(reset));
  Multiplexer #(.select(5), .width(32)) multiplexer_2 (
    .in0(o0), .in1(o1), .in2(o2), .in3(o3), .in4(o4), .in5(o5), .in6(o6), .in7(o7), .in8(o8), .in9(o9),
    .in10(o10), .in11(o11), .in12(o12), .in13(o13), .in14(o14), .in15(o15), .in16(o16), .in17(o17),
    .in18(o18), .in19(o19), .in20(o20), .in21(o21), .in22(o22), .in23(o23), .in24(o24), .in25(o25),
    .in26(o26), .in27(o27), .in28(o28), .in29(o29), .in30(o30), .in31(o31), .out(busB), .sel(RB),
    .en(undriven_2));
  Register #(.width(32)) register_29 (.D(i7), .en(RegWr), .Q(o7), .clk(clk), .clr(reset));
  Register #(.width(32)) register_30 (.D(i15), .en(RegWr), .Q(o15), .clk(clk), .clr(reset));
  Register #(.width(32)) register_31 (.D(i23), .en(RegWr), .Q(o23), .clk(clk), .clr(reset));
  Register #(.width(32)) register_32 (.D(i31), .en(RegWr), .Q(o31), .clk(clk), .clr(reset));
endmodule

module ALU (
  input  [2:0] ALUctr,
  input  [31:0] ALUin1,
  input  [31:0] ALUin1_prime,
  input  [31:0] ALUin2,
  input  sll,
  output zero,
  output [31:0] ALUOut
);

  wire comparator_2_lt;
  wire [31:0] adder_1_out, bit_extender_1_out, multiplexer_1_out, or_1_out, shifter_1_out, subtractor_1_out;

  Multiplexer #(.width(32)) multiplexer_1 (
    .in0(ALUin1), .in1(ALUin1_prime), .out(multiplexer_1_out), .sel(sll));  // open: en
  Comparator #(.width(32), .mode("unsigned")) comparator_1 (
    .a(multiplexer_1_out), .b(ALUin2), .eq(zero));  // open: gt, lt
  Adder #(.width(32)) adder_1 (.a(multiplexer_1_out), .b(ALUin2), .out(adder_1_out));  // open: cin, cout
  Subtractor #(.width(32)) subtractor_1 (.a(multiplexer_1_out), .b(ALUin2), .out(subtractor_1_out));  // open: bin, bout
  assign or_1_out = multiplexer_1_out | ALUin2;  // OR_Gate or_1, 32 bits wide
  Shifter #(.width(32)) shifter_1 (.in(multiplexer_1_out), .\dist (ALUin2[10:6]), .out(shifter_1_out));
  Comparator #(.width(32)) comparator_2 (.a(multiplexer_1_out), .b(ALUin2), .lt(comparator_2_lt));  // open: gt, eq
  assign bit_extender_1_out = {{31{1'b0}}, comparator_2_lt};  // Bit_Extender bit_extender_1
  Multiplexer #(.select(3), .width(32)) multiplexer_2 (
    .in0(adder_1_out), .in1(subtractor_1_out), .in2(or_1_out), .in3(shifter_1_out), .in4(bit_extender_1_out),
    .out(ALUOut), .sel(ALUctr));  // open: in5, in6, in7, en
endmodule

module DM (
  input  [31:0] DMaddr,
  input  sb,
  input  MemWr,
  input  lb,
  input  [31:0] DMdata,
  input  clk,
  input  reset,
  output [31:0] DMOut
);

  wire [7:0] _7_0, _15_8, _23_16, _31_24;
  wire [31:0] bit_extender_1_out, bit_extender_2_out, bit_extender_3_out, bit_extender_4_out,
       multiplexer_1_out, multiplexer_2_out, multiplexer_4_out;

  Multiplexer #(.select(2), .width(32)) multiplexer_1 (
    .in0({_31_24, _23_16, _15_8, DMdata[7:0]}), .in1({_31_24, _23_16, DMdata[7:0], _7_0}),
    .in2({_31_24, DMdata[7:0], _15_8, _7_0}), .in3({DMdata[7:0], _23_16, _15_8, _7_0}),
    .out(multiplexer_1_out), .sel(DMaddr[1:0]));  // open: en
  Multiplexer #(.width(32)) multiplexer_2 (
    .in0(DMdata), .in1(multiplexer_1_out), .out(multiplexer_2_out), .sel(sb));  // open: en
  RAM #(.addrWidth(5), .dataWidth(32), .bus("separate")) ram_1 (
    .addr(DMaddr[6:2]), .din(multiplexer_2_out), .data({_31_24, _23_16, _15_8, _7_0}), .str(MemWr),
    .clk(clk), .ld(1'b1), .clr(reset));  // open: sel
  assign bit_extender_1_out = {{24{_7_0[7]}}, _7_0};  // Bit_Extender bit_extender_1
  assign bit_extender_2_out = {{24{_15_8[7]}}, _15_8};  // Bit_Extender bit_extender_2
  assign bit_extender_3_out = {{24{_23_16[7]}}, _23_16};  // Bit_Extender bit_extender_3
  assign bit_extender_4_out = {{24{_31_24[7]}}, _31_24};  // Bit_Extender bit_extender_4
  Multiplexer #(.width(32)) multiplexer_3 (
    .in0({_31_24, _23_16, _15_8, _7_0}), .in1(multiplexer_4_out), .out(DMOut), .sel(lb));  // open: en
  Multiplexer #(.select(2), .width(32)) multiplexer_4 (
    .in0(bit_extender_1_out), .in1(bit_extender_2_out), .in2(bit_extender_3_out), .in3(bit_extender_4_out),
    .out(multiplexer_4_out), .sel(DMaddr[1:0]));  // open: en

  // Other names for the same wires on the sheet: data_byte[7:0] = DMdata[7:0]; addr[1:0] = DMaddr[1:0]
endmodule

module EXT (
  input  [15:0] imm16,
  input  [1:0] ExtOp,
  output [31:0] out_3
);

  wire [31:0] bit_extender_1_out, bit_extender_2_out;

  assign bit_extender_1_out = {{16{1'b0}}, imm16};  // Bit_Extender bit_extender_1
  assign bit_extender_2_out = {{16{imm16[15]}}, imm16};  // Bit_Extender bit_extender_2
  Multiplexer #(.select(2), .width(32)) multiplexer_1 (
    .in0(bit_extender_1_out), .in1(bit_extender_2_out), .in2({imm16, {16{1'b0}}}), .out(out_3), .sel(ExtOp));  // open: in3, en
endmodule

module Controller_OR (
  input  addu,
  input  subu,
  input  ori,
  input  lw,
  input  sw,
  input  beq,
  input  lui,
  input  sll,
  input  addi,
  input  j,
  input  jal,
  input  jr,
  input  jalr,
  input  slt,
  input  sb,
  input  lb,
  output ALUSrc,
  output nPC_sel,
  output MemWr,
  output MemtoReg,
  output RegDst,
  output RegWr,
  output [1:0] ExtOp,
  output [2:0] ALUctr,
  output jump,
  output jal_r,
  output sll_2,
  output jr_2,
  output jal_2,
  output sb_2,
  output lb_2
);

  or u_ALUSrc (ALUSrc, sb, ori, lw, sw, lui, sll, addi, lb);
  buf u_nPC_sel (nPC_sel, beq);  // OR_Gate
  or u_MemWr (MemWr, sw, sb);
  or u_MemtoReg (MemtoReg, lw, lb);
  or u_RegDst (RegDst, addu, subu, sll, jalr, slt);
  or u_RegWr (RegWr, slt, jalr, addi, addu, subu, ori, lw, lui, sll, jal, lb);
  buf ExtOp_1 (ExtOp[1], lui);  // OR_Gate
  or ExtOp_0 (ExtOp[0], lw, sw, addi, sb, lb);
  buf ALUctr_2 (ALUctr[2], slt);  // OR_Gate
  or ALUctr_1 (ALUctr[1], ori, sll);
  or ALUctr_0 (ALUctr[0], subu, sll);
  buf u_jal (jal_2, jal);  // OR_Gate
  or u_jump (jump, j, jal);
  or u_jal_r (jal_r, jal, jalr);
  or u_jr (jr_2, jr, jalr);
  buf u_sll (sll_2, sll);  // OR_Gate
  buf u_sb (sb_2, sb);  // OR_Gate
  buf u_lb (lb_2, lb);  // OR_Gate
endmodule

module Controller_AND (
  input  [5:0] opcode,
  input  [5:0] funct,
  output addu,
  output subu,
  output ori,
  output lw,
  output sw,
  output beq,
  output lui,
  output sll,
  output addi,
  output j,
  output jal,
  output jr,
  output jalr,
  output slt,
  output sb,
  output lb
);

  wire not_1_out, not_2_out, not_3_out, not_4_out, not_5_out, not_6_out, not_7_out, not_8_out, not_9_out,
       not_10_out, not_11_out, not_12_out, Rtype;

  not not_1 (not_1_out, opcode[5]);
  not not_2 (not_2_out, opcode[4]);
  not not_3 (not_3_out, opcode[2]);
  not not_4 (not_4_out, opcode[3]);
  not not_5 (not_5_out, opcode[1]);
  not not_6 (not_6_out, opcode[0]);
  and u_Rtype (Rtype, not_1_out, not_2_out, not_4_out, not_3_out, not_5_out, not_6_out);
  and u_ori (ori, not_1_out, not_2_out, opcode[3], opcode[2], not_5_out, opcode[0]);
  and u_lw (lw, opcode[5], not_2_out, not_4_out, not_3_out, opcode[1], opcode[0]);
  and u_sw (sw, opcode[5], not_2_out, opcode[3], not_3_out, opcode[1], opcode[0]);
  and u_beq (beq, not_1_out, not_2_out, not_4_out, opcode[2], not_5_out, not_6_out);
  and u_lui (lui, not_1_out, not_2_out, opcode[3], opcode[2], opcode[1], opcode[0]);
  and u_addi (addi, not_1_out, not_2_out, opcode[3], not_3_out, not_5_out, not_6_out);
  and u_j (j, not_1_out, not_2_out, not_4_out, not_3_out, opcode[1], not_6_out);
  and u_jal (jal, not_1_out, not_2_out, not_4_out, not_3_out, opcode[1], opcode[0]);
  and u_sb (sb, opcode[5], not_2_out, opcode[3], not_3_out, not_5_out, not_6_out);
  and u_lb (lb, opcode[5], not_2_out, not_4_out, not_3_out, not_5_out, not_6_out);
  not not_7 (not_7_out, funct[5]);
  not not_8 (not_8_out, funct[3]);
  not not_9 (not_9_out, funct[4]);
  not not_10 (not_10_out, funct[2]);
  not not_11 (not_11_out, funct[1]);
  not not_12 (not_12_out, funct[0]);
  and u_addu (addu, funct[5], not_9_out, not_8_out, not_10_out, not_11_out, funct[0], Rtype);
  and u_subu (subu, funct[5], not_9_out, not_8_out, not_10_out, funct[1], funct[0], Rtype);
  and u_sll (sll, not_7_out, not_9_out, not_8_out, not_10_out, not_11_out, not_12_out, Rtype);
  and u_jr (jr, not_7_out, not_9_out, funct[3], not_10_out, not_11_out, not_12_out, Rtype);
  and u_jalr (jalr, not_7_out, not_9_out, funct[3], not_10_out, not_11_out, funct[0], Rtype);
  and u_slt (slt, funct[5], not_9_out, funct[3], not_10_out, funct[1], not_12_out, Rtype);

  // Other names for the same wires on the sheet: f0 = funct[0]; f1 = funct[1]; f2 = funct[2]; f3 = funct[3];
  //   f4 = funct[4]; f5 = funct[5]; op0 = opcode[0]; op1 = opcode[1]; op2 = opcode[2]; op3 = opcode[3];
  //   op4 = opcode[4]; op5 = opcode[5]
endmodule

module Controller (
  input  [5:0] opcode,
  input  [5:0] funct,
  output ALUSrc,
  output nPC_sel,
  output MemWr,
  output MemtoReg,
  output RegDst,
  output RegWr,
  output [1:0] ExtOp,
  output [2:0] ALUctr,
  output jump,
  output jal_r,
  output sll,
  output jr,
  output jal,
  output sb,
  output lb
);

  wire controller_and_1_addi, controller_and_1_addu, controller_and_1_beq, controller_and_1_j,
       controller_and_1_jal, controller_and_1_jalr, controller_and_1_jr, controller_and_1_lb,
       controller_and_1_lui, controller_and_1_lw, controller_and_1_ori, controller_and_1_sb,
       controller_and_1_sll, controller_and_1_slt, controller_and_1_subu, controller_and_1_sw;

  Controller_AND controller_and_1 (
    .opcode(opcode), .funct(funct), .addu(controller_and_1_addu), .subu(controller_and_1_subu),
    .ori(controller_and_1_ori), .lw(controller_and_1_lw), .sw(controller_and_1_sw),
    .beq(controller_and_1_beq), .lui(controller_and_1_lui), .sll(controller_and_1_sll),
    .addi(controller_and_1_addi), .j(controller_and_1_j), .jal(controller_and_1_jal),
    .jr(controller_and_1_jr), .jalr(controller_and_1_jalr), .slt(controller_and_1_slt),
    .sb(controller_and_1_sb), .lb(controller_and_1_lb));
  Controller_OR controller_or_1 (
    .addu(controller_and_1_addu), .subu(controller_and_1_subu), .ori(controller_and_1_ori),
    .lw(controller_and_1_lw), .sw(controller_and_1_sw), .beq(controller_and_1_beq),
    .lui(controller_and_1_lui), .sll(controller_and_1_sll), .addi(controller_and_1_addi),
    .j(controller_and_1_j), .jal(controller_and_1_jal), .jr(controller_and_1_jr),
    .jalr(controller_and_1_jalr), .slt(controller_and_1_slt), .sb(controller_and_1_sb),
    .lb(controller_and_1_lb), .ALUSrc(ALUSrc), .nPC_sel(nPC_sel), .MemWr(MemWr), .MemtoReg(MemtoReg),
    .RegDst(RegDst), .RegWr(RegWr), .ExtOp(ExtOp), .ALUctr(ALUctr), .jump(jump), .jal_r(jal_r), .sll_2(sll),
    .jr_2(jr), .jal_2(jal), .sb_2(sb), .lb_2(lb));
endmodule
